# Fritzing sketch ESP32-S3DK-I2CTest (saved by Fritzing 0.9.5d)
breadboards: 2

parts:
  ESP32-S3-DEVKIT1 = ESP32-S3-DEVKIT [part_number=ESP32-S3-DEVKIT]
  Universal_LCC_Node_Breakout1 = UniversalLCCNodeBreakout

nets:
  3.3V: ESP32-S3-DEVKIT1.connector6, ESP32-S3-DEVKIT1.connector7, Universal_LCC_Node_Breakout1.connector1
  CAN RX: ESP32-S3-DEVKIT1.connector9, Universal_LCC_Node_Breakout1.connector2
  CAN TX: ESP32-S3-DEVKIT1.connector10, Universal_LCC_Node_Breakout1.connector3
  5V: ESP32-S3-DEVKIT1.connector26, Universal_LCC_Node_Breakout1.connector0
  GND: ESP32-S3-DEVKIT1.connector27, ESP32-S3-DEVKIT1.connector28, ESP32-S3-DEVKIT1.connector29, ESP32-S3-DEVKIT1.connector49, Universal_LCC_Node_Breakout1.connector4
